# Fritzing sketch circuit-digram (saved by Fritzing 0.9.9b)
breadboards: 1

parts:
  U1 = NodeMCU V1.0
  S1 = Pushbutton [package="[THT]"]
  S2 = Pushbutton [package="[THT]"]
  S3 = Pushbutton [package="[THT]"]
  S4 = Pushbutton [package="[THT]"]
  LED1 = LED - 5mm [color="Red (633nm)" current=0.030 package="5 mm [THT]"]
  LED2 = LED - 5mm [color="Red (633nm)" current=0.030 package="5 mm [THT]"]
  LED3 = LED - 5mm [color="Red (633nm)" current=0.030 package="5 mm [THT]"]
  LED4 = LED - 5mm [color="Red (633nm)" current=0.030 package="5 mm [THT]"]
  R1 = Resistor [tolerance=±5% power=0.25 resistance=220 package=THT]
  R2 = Resistor [tolerance=±5% power=0.25 resistance=220 package=THT]
  R3 = Resistor [tolerance=±5% power=0.25 resistance=220 package=THT]
  R4 = Resistor [tolerance=±5% power=0.25 resistance=220 package=THT]
  R5 = Resistor [tolerance=±5% power=0.25 resistance=220 package=THT]
  R6 = Resistor [tolerance=±5% power=0.25 resistance=220 package=THT]
  R7 = Resistor [tolerance=±5% power=0.25 resistance=220 package=THT]
  R8 = Resistor [tolerance=±5% power=0.25 resistance=220 package=THT]

nets:
  N1: U1.D0, S1.Pin_3, S1.Pin_4, R1.Pin_0
  N2: U1.D1, S2.Pin_3, S2.Pin_4, R2.Pin_0
  N3: U1.D2, S3.Pin_3, S3.Pin_4, R3.Pin_0
  N4: U1.D3, S4.Pin_3, S4.Pin_4, R4.Pin_0
  N5: U1.3V3, S1.Pin_1, S1.Pin_2, S2.Pin_1, S2.Pin_2, S3.Pin_1, S3.Pin_2, S4.Pin_1, S4.Pin_2
  N6: U1.GND, R1.Pin_1, R2.Pin_1, R3.Pin_1, R4.Pin_1, R5.Pin_1, R6.Pin_1, R7.Pin_1, R8.Pin_1
  N7: U1.D5, LED1.anode
  N8: U1.D6, LED2.anode
  N9: U1.D7, LED3.anode
  N10: U1.D8, LED4.anode
  N11: LED1.cathode, R5.Pin_0
  N12: LED2.cathode, R6.Pin_0
  N13: LED3.cathode, R7.Pin_0
  N14: LED4.cathode, R8.Pin_0

custom parts:
  NodeMCU V1.0: ESP8266 based NodeMCU
